// Logisim project guia_07.circ as structural Verilog: 1 circuit, main circuit main
module main (
  input  x,
  input  x_2,
  input  y,
  input  y_2,
  input  e,
  input  e_2,
  input  x_3,
  input  y_3,
  input  e_3,
  input  e_4,
  input  x_4,
  input  y_4,
  input  e1,
  input  e0,
  input  x_5,
  input  y_5,
  input  e2,
  input  e1_2,
  input  e0_2,
  output out_20,
  output out_21,
  output out_22,
  output out_23,
  output out_24,
  output out_25
);

  wire and_1_out, and_2_out, and_3_out, and_4_out, and_5_out, and_6_out, and_7_out, and_8_out, and_9_out,
       and_10_out, and_11_out, and_12_out, and_13_out, and_14_out, and_15_out, and_16_out, and_17_out,
       and_18_out, and_19_out, and_20_out, and_21_out, and_22_out, and_23_out, and_24_out, and_25_out,
       and_26_out, nand_1_out, nand_2_out, nand_3_out, nand_4_out, nand_5_out, nor_1_out, nor_2_out,
       nor_3_out, nor_4_out, nor_5_out, nor_6_out, not_1_out, not_2_out, not_3_out, not_4_out, not_5_out,
       not_6_out, not_7_out, not_8_out, not_9_out, not_10_out, or_1_out, or_2_out, or_3_out, or_7_out,
       xnor_1_out, xnor_2_out, xor_1_out, xor_2_out;

  and and_1 (and_1_out, x, y);
  nand nand_1 (nand_1_out, x, y);
  and and_2 (and_2_out, x_3, y_3);
  nand nand_2 (nand_2_out, x_3, y_3);
  or or_1 (or_1_out, x_3, y_3);
  nor nor_1 (nor_1_out, x_3, y_3);
  nand nand_3 (nand_3_out, nand_1_out, nand_1_out);
  not not_1 (not_1_out, e);
  nand nand_4 (nand_4_out, nand_2_out, nand_2_out);
  nor nor_2 (nor_2_out, nor_1_out, nor_1_out);
  not not_2 (not_2_out, e_3);
  xor xor_1 (xor_1_out, x_4, y_4);
  xnor xnor_1 (xnor_1_out, x_4, y_4);
  or or_2 (or_2_out, x_4, y_4);
  nor nor_3 (nor_3_out, x_4, y_4);
  not not_3 (not_3_out, x_5);
  and and_3 (and_3_out, x_5, y_5);
  nand nand_5 (nand_5_out, x_5, y_5);
  xor xor_2 (xor_2_out, x_5, y_5);
  xnor xnor_2 (xnor_2_out, x_5, y_5);
  or or_3 (or_3_out, x_5, y_5);
  nor nor_4 (nor_4_out, x_5, y_5);
  and and_4 (and_4_out, and_1_out, not_1_out);
  and and_5 (and_5_out, nand_3_out, e);
  not not_4 (not_4_out, e0);
  not not_5 (not_5_out, e1);
  not not_6 (not_6_out, e2);
  or or_4 (out_20, and_4_out, and_5_out);
  and and_6 (and_6_out, and_2_out, not_2_out);
  and and_7 (and_7_out, nand_4_out, e_3);
  and and_8 (and_8_out, or_1_out, not_2_out);
  and and_9 (and_9_out, nor_2_out, e_3);
  and and_10 (and_10_out, xor_1_out, not_5_out, not_4_out);
  and and_11 (and_11_out, xnor_1_out, not_5_out, e0);
  and and_12 (and_12_out, or_2_out, e1, not_4_out);
  and and_13 (and_13_out, nor_3_out, e1, e0);
  not not_7 (not_7_out, e1_2);
  not not_8 (not_8_out, e0_2);
  or or_5 (out_23, and_6_out, and_7_out, and_8_out, and_9_out);
  or or_6 (out_24, and_10_out, and_11_out, and_12_out, and_13_out);
  and and_14 (and_14_out, not_3_out, not_6_out, not_7_out, not_8_out);
  and and_15 (and_15_out, and_3_out, not_6_out, not_7_out, e0_2);
  and and_16 (and_16_out, nand_5_out, not_6_out, e1_2, not_8_out);
  and and_17 (and_17_out, xor_2_out, not_6_out, e1_2, e0_2);
  and and_18 (and_18_out, xnor_2_out, e2, not_7_out, not_8_out);
  and and_19 (and_19_out, or_3_out, e2, not_7_out, e0_2);
  and and_20 (and_20_out, nor_4_out, e2, e1_2, not_8_out);
  or or_7 (or_7_out, x_2, y_2);
  nor nor_5 (nor_5_out, x_2, y_2);
  not not_9 (not_9_out, e_4);
  nor nor_6 (nor_6_out, nor_5_out, nor_5_out);
  not not_10 (not_10_out, e_2);
  and and_21 (and_21_out, and_6_out, not_9_out);
  and and_22 (and_22_out, and_7_out, not_9_out);
  and and_23 (and_23_out, and_8_out, e_4);
  and and_24 (and_24_out, and_9_out, e_4);
  or or_8 (out_25, and_14_out, and_15_out, and_16_out, and_17_out, and_18_out, and_19_out, and_20_out);
  and and_25 (and_25_out, or_7_out, not_10_out);
  or or_9 (out_21, and_25_out, and_26_out);
  and and_26 (and_26_out, nor_6_out, e_2);
  or or_10 (out_22, and_21_out, and_22_out, and_23_out, and_24_out);

  // Notes on the sheet:
  //   GUIA_0701
  //   GUIA_0703
  //   GUIA_0704
  //   GUIA_0705
  //   0 AND/OR
  //   1 NAND/NOR
  //   AND
  //   NAND
  //   OR
  //   NOR
  //   GUIA_0702
  //   NOT
  //   AND
  //   NAND
  //   XOR
  //   XNOR
  //   OR
  //   NOR
  //   AND
  //   NAND
  //   OR
  //   NOR
  //   0 AND/NAND
  //   1 OR/NOR
endmodule
